# Fritzing sketch sketch (saved by Fritzing 0.9.9b)

parts:
  U1 = ESP8266 NodeMCU LoLin module
  DFRobot_DFPlayer_Mini1 = DFRobot DFPlayer Mini [part_number=DFR0299]
  SP1 = SPEAKER [package=pcb_mount_speaker]
  U2 = POT [package=alps_pot]
  HC-SR04_Sensor_1 = HC-SR04 Ultrasonic Distance Sensor

nets:
  N1: U1.D2, HC-SR04_Sensor_1.TRIG
  N2: U1.D3, HC-SR04_Sensor_1.ECHO
  N3: U1.D5, DFRobot_DFPlayer_Mini1.TX
  N4: U1.D6, DFRobot_DFPlayer_Mini1.RX
  N5: U1.A0, U2.S
  N6: DFRobot_DFPlayer_Mini1.SPK_1, SP1.+
  N7: DFRobot_DFPlayer_Mini1.SPK_2, SP1.-

custom parts:
  ESP8266 NodeMCU LoLin module: ESP8266 based NodeMCU
